# Fritzing sketch esp_piscine (saved by Fritzing 0.9.3b)

parts:
  R1 = Resistor [tolerance=±5% resistance=4.7k package=THT]  # not connected
  S3 = Magnetic Door Switch [package=reed_switch_plastic]
  R3 = Resistor [tolerance=±5% resistance=10k package="2512 [SMD]"]  # not connected
  MH-ET_LIVE_ESP32_DEVKIT1 = MH-ET LIVE ESP32 DEVKIT 38 pins
  U2 = 4RelayModule  # not connected
  Composant1 = BME280  # not connected
  DS1 = DS18B20 1-Wire Temperature Sensor [part_number=DS18B20]  # not connected
  DS2 = DS18B20 1-Wire Temperature Sensor [part_number=DS18B20]  # not connected
  DS3 = DS18B20 1-Wire Temperature Sensor [part_number=DS18B20]  # not connected
  M1 = Pzem-004t  # not connected
  Squix1 = OLED 0.96" 128x64 I2C SSD1306  # not connected

nets:
  N1: S3.2, MH-ET_LIVE_ESP32_DEVKIT1.IO16

notes:
  ESP32 + ESPHOME / HA
  4.7K
  magnetic door or window sensor
  10K

custom parts:
  MH-ET LIVE ESP32 DEVKIT 38 pins: http://mh.nodebb.com/topic/2/mh-et-live-esp32-devkit
  4RelayModule: 4 relay arduino module SONGLE SRD05VDC-SL-C
  Pzem-004t: Pzem-004t used for measuring AC voltage, current, active power, frequency, power factor and active energy, the module is without display function, the data is read through the TTL interface.
